# Fritzing sketch Robot (saved by Fritzing 0.9.10b)
breadboards: 1

parts:
  J1 = Piezo Speaker
  M3 = DC Motor [voltage_(max)=6V voltage_(min)=3V]
  M6 = DC Motor [voltage_(max)=6V voltage_(min)=3V]
  U1 = WS2812 RGB LED strip
  Mod2 = HC-SR04 Ultrasonic Distance Sensor
  L298N1 = L298N DC motor driver
  TFT1 = Color 320x240 TFT Display, ILI9341 Controller Chip
  A1 = usbc to 12V module
  M7 = ESP32-S2-DevKitC-1 [part_number=ESP32-S2-DevKitC-1]

nets:
  GND: J1.pin1, U1.GND, Mod2.GND, L298N1.12V, L298N1.GND, TFT1.GND, A1.Pin_3, A1.Pin_4, M7.pin_22, M7.pin_23, M7.pin_24, M7.pin_44
  N1: J1.pin2, M7.pin_27
  N2: M3.pin_1, L298N1.OUT3
  N3: M3.pin_2, L298N1.OUT4
  N4: M6.pin_1, L298N1.OUT2
  N5: M6.pin_2, L298N1.OUT1
  VCC: U1.VCC, Mod2.VCC, L298N1.5V, TFT1.VCC, TFT1.LED, M7.pin_21
  N6: U1.DIN, M7.pin_39
  N7: Mod2.TRIG, M7.pin_37
  N8: Mod2.ECHO, M7.pin_42
  N9: L298N1.ENA, M7.pin_28
  N10: L298N1.ENB, M7.pin_29
  N11: L298N1.IN1, M7.pin_36
  N12: L298N1.IN2, M7.pin_35
  N13: L298N1.IN3, M7.pin_43
  N14: L298N1.IN4, M7.pin_33
  N15: TFT1.CS, M7.pin_16
  N16: TFT1.Reset, M7.pin_12
  N17: TFT1.D/C, M7.pin_13
  N18: TFT1.SDI_(MOSI), M7.pin_17
  N19: TFT1.SCK, M7.pin_18
  N20: M7.pin_1, M7.pin_2

notes:
  Buzzer
  DC Motor
  L298N
  Neopixel
  HC-SR04
  ESP32 S3
  5 Volt from ESP32
  ili9341
  9 Volt USB-C

custom parts:
  WS2812 RGB LED strip: WS2812 strip
  L298N DC motor driver: 2x DC motor driver with 78M05 positive voltage regulator (7..35 V) L298N: max 46 V, 2 A Set 5 V Enable jumper to enable 5 V regultor (needed for the L298N) and +5 V output at screw terminal or supply external +5 V at screw terminal Set ENA and/or ENB to +5 V to enable motor permanently or supply ENA and/or ENB with PWM signal IN1 and IN2 set rotation directory for motor A (OUT1/OUT2) IN2 and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
  Color 320x240 TFT Display, ILI9341 Controller Chip: 2.2" TFT Display with ILI9341 Controller
  usbc to 12V module: usbc to 12V module.
  ESP32-S2-DevKitC-1: ESP32-S2-DevKitC-1 is an entry-level development board based on ESP32-S2-SOLO (on-board PCB antenna). It is based on the ESP32 microcontroller that boasts Wifi, Bluetooth, Ethernet and Low Power support all in a single chip. (vanepp) Feb 2022: converted to ESP32-S2-DevKitC-1. This module is 44pins long (2x22) and 11 pins width.
